# Fritzing sketch Robot_Head_Schematics (saved by Fritzing 0.9.3b)
breadboards: 1

parts:
  Part1 = Arduino Uno (Rev3) - ICSP
  J1 = Basic Servo
  HC-SR04_Sensor_right = HC-SR04 Ultrasonic Distance Sensor
  HC-SR04_Sensor_2 = HC-SR04 Ultrasonic Distance Sensor
  8x8_LED_Modul_mit_MAX1 = 8x8 LED Modul mit MAX7219 [package=THT]
  8x8_LED_Modul_mit_MAX2 = 8x8 LED Modul mit MAX7219 [package=THT]

nets:
  N1: Part1.D9_PWM, J1.pulse
  N2: Part1.D10_PWM/SS, HC-SR04_Sensor_2.TRIG
  N3: Part1.D11_PWM/MOSI, HC-SR04_Sensor_2.ECHO
  N4: Part1.D2, HC-SR04_Sensor_right.TRIG
  N5: Part1.D3_PWM, HC-SR04_Sensor_right.ECHO
  N6: Part1.D5_PWM, 8x8_LED_Modul_mit_MAX1.CLK_Eingang
  N7: Part1.D6_PWM, 8x8_LED_Modul_mit_MAX1.CS_Eingang
  N8: Part1.D7, 8x8_LED_Modul_mit_MAX1.DIN_Eingang
  VCC: Part1.5V, J1.vcc, HC-SR04_Sensor_right.VCC, HC-SR04_Sensor_2.VCC, 8x8_LED_Modul_mit_MAX1.VCC_Eingang
  GND: Part1.GND, J1.gnd, HC-SR04_Sensor_right.GND, HC-SR04_Sensor_2.GND, 8x8_LED_Modul_mit_MAX1.GND_Eingang
  N9: 8x8_LED_Modul_mit_MAX1.VCC_Ausgang, 8x8_LED_Modul_mit_MAX2.VCC_Eingang
  N10: 8x8_LED_Modul_mit_MAX1.GND_Ausgang, 8x8_LED_Modul_mit_MAX2.GND_Eingang
  N11: 8x8_LED_Modul_mit_MAX1.DOUT_Ausgang, 8x8_LED_Modul_mit_MAX2.DIN_Eingang
  N12: 8x8_LED_Modul_mit_MAX1.CS_Ausgang, 8x8_LED_Modul_mit_MAX2.CS_Eingang
  N13: 8x8_LED_Modul_mit_MAX1.CLK_Ausgang, 8x8_LED_Modul_mit_MAX2.CLK_Eingang

notes:
  sensor_left
  trig_lf =10
  echo_lf= 11
  sensor_right
  trig_ri =2
  echo_ri= 3
  led_max_7219
  DIN = 7
  CLK = 5
  CS = 6
  servo
  pulse=9
