# Fritzing sketch Self_Balance_Robot_Schematics (saved by Fritzing 0.9.3b)
breadboards: 1

parts:
  Part1 = Arduino Nano (Rev3.0)
  L298N1 = L298N DC motor driver
  Part2 = Bluetooth HC-05 Macho
  M2 = gear-motor
  M3 = gear-motor
  Part3 = InvenSense MPU6050
  U1 = LIPO-2000mAh [package=lipo-2000]

nets:
  N1: Part1.D2, Part3.INT
  N2: Part1.D3, L298N1.IN4
  N3: Part1.D5, Part2.TXD
  N4: Part1.D6, Part2.RXD
  N5: Part1.D9, L298N1.IN3
  N6: Part1.D10, L298N1.IN2
  N7: Part1.D11/MOSI, L298N1.IN1
  GND: Part1.GND, Part2.GND
  5V: Part1.5V, L298N1.5V, Part2.VCC, Part3.VCC
  N8: Part1.A5, Part3.SCL
  N9: Part1.A4, Part3.SDA
  N10: L298N1.OUT1, M2.pin_2
  N11: L298N1.OUT2, M2.pin_1
  N12: L298N1.OUT3, M3.pin_2
  N13: L298N1.OUT4, M3.pin_1
  N14: L298N1.12V, U1.+
  N15: L298N1.GND, U1.-

notes:
  bluetooth
  txpin = 5
  rxpin = 6
  mpu6050
  scl=A5
  sda=A4
  L298N
  IN1 =11
  IN2 =10
  IN3 =9
  IN4 =3

custom parts:
  L298N DC motor driver: 2x DC motor driver with 78M05 positive voltage regulator (7..35 V) L298N: max 46 V, 2 A Set 5 V Enable jumper to enable 5 V regultor (needed for the L298N) and +5 V output at screw terminal or supply external +5 V at screw terminal Set ENA and/or ENB to +5 V to enable motor permanently or supply ENA and/or ENB with PWM signal IN1 and IN2 set rotation directory for motor A (OUT1/OUT2) IN2 and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
